// Logisim project basics_logic_gates.circ as structural Verilog
module transistor_basics (
  input  in_1,
  output out_2,
  output out_3
);

  Transistor transistor_1 (.in(1'b1), .out(out_2), .gate(in_1));
  Transistor #(.\type ("n")) transistor_2 (.in(1'b0), .out(out_3), .gate(in_1));

  // Notes on the sheet:
  //   P-type transistors allow current to flow when the gate voltage (left) is lower than the source voltage (top)
  //   N-type transistors allow current to flow when the gate voltage (left) is higher than the source voltage (bottom)
  //   P-type transistors are also known as PMOS transistors, and N-type as NMOS. CMOS circuits use both
  //   The advantages of CMOS are reduced power consumption and better noise characteristics, when compared to PMOS-only or NMOS-only logic
endmodule

module not_gate_nmos (
  input  in_1,
  output out_2
);

  Pull_Resistor #(.pull(1)) pull_resistor_1 (.node(out_2));
  Transistor #(.\type ("n")) transistor_1 (.in(1'b0), .out(out_2), .gate(in_1));

  // Notes on the sheet:
  //   NOT is the simplest logic gate. Shown here is a NOT gate constructed using only a single NMOS transistor
  //   When the input is 0 the circuit is closed, and the output is directly connected to power through a pullup resistor
  //   When the input is 1, current flows from power to ground through the resistor. Voltage drops to 0 across the resistor
  //   While this design is simple and requires only a single transistor, the circuit draws constant power when the transistor is open
endmodule

module not_gate_cmos (
  input  in_1,
  output out_2
);

  Transistor transistor_1 (.in(1'b1), .out(out_2), .gate(in_1));
  Transistor #(.\type ("n")) transistor_2 (.in(1'b0), .out(out_2), .gate(in_1));

  // Notes on the sheet:
  //   The CMOS NOT gate behaves identically to an NMOS or PMOS NOT gate, except there is no path from power to ground
  //   This means that a CMOS NOT gate does not draw any power in a static state. Power is only consumed when the state changes
  //   CMOS gates are the norm in most logic circuits. NMOS and PMOS circuits are still used in some cases, e.g. monitor displays
endmodule

module nand_gate_cmos (
  input  in_1,
  input  in_2,
  input  in_3,
  input  in_4,
  input  in_5,
  output out_6,
  output out_7
);

  wire transistor_3_out, transistor_7_out, transistor_8_out;

  Transistor transistor_1 (.in(1'b1), .out(out_6), .gate(in_2));
  Transistor #(.\type ("n")) transistor_2 (.in(transistor_3_out), .out(out_6), .gate(in_2));
  Transistor #(.\type ("n")) transistor_3 (.in(1'b0), .out(transistor_3_out), .gate(in_4));
  Transistor transistor_4 (.in(1'b1), .out(out_6), .gate(in_4));
  Transistor transistor_5 (.in(1'b1), .out(out_7), .gate(in_1));
  Transistor #(.\type ("n")) transistor_6 (.in(transistor_7_out), .out(out_7), .gate(in_1));
  Transistor #(.\type ("n")) transistor_7 (.in(transistor_8_out), .out(transistor_7_out), .gate(in_3));
  Transistor #(.\type ("n")) transistor_8 (.in(1'b0), .out(transistor_8_out), .gate(in_5));
  Transistor transistor_9 (.in(1'b1), .out(out_7), .gate(in_3));
  Transistor transistor_10 (.in(1'b1), .out(out_7), .gate(in_5));

  // Notes on the sheet:
  //   Two input NAND gate
  //   Three input NAND gate
  //   Can be generalized to any number of inputs
  //   All NMOS in parallel
  //   All PMOS in parallel
endmodule

module nor_gate_cmos (
  input  in_1,
  input  in_2,
  output out_3
);

  wire transistor_1_out;

  Transistor transistor_1 (.in(1'b1), .out(transistor_1_out), .gate(in_1));
  Transistor transistor_2 (.in(transistor_1_out), .out(out_3), .gate(in_2));
  Transistor #(.\type ("n")) transistor_3 (.in(1'b0), .out(out_3), .gate(in_2));
  Transistor #(.\type ("n")) transistor_4 (.in(1'b0), .out(out_3), .gate(in_1));

  // Notes on the sheet:
  //   Two input NOR gate
  //   PMOS in series
  //   NMOS in parallel
endmodule

module xor_gate_cmos (
  input  in_1,
  input  in_2,
  output out_3
);

  wire not_gate_nmos_1_out_2, not_gate_nmos_2_out_2, transistor_1_out, transistor_7_out;

  not_gate_nmos not_gate_nmos_1 (.in_1(in_1), .out_2(not_gate_nmos_1_out_2));
  not_gate_nmos not_gate_nmos_2 (.in_1(in_2), .out_2(not_gate_nmos_2_out_2));
  Transistor transistor_1 (.in(1'b1), .out(transistor_1_out), .gate(not_gate_nmos_1_out_2));
  Transistor transistor_2 (.in(1'b1), .out(transistor_1_out), .gate(not_gate_nmos_2_out_2));
  Transistor transistor_3 (.in(transistor_1_out), .out(out_3), .gate(in_1));
  Transistor transistor_4 (.in(transistor_1_out), .out(out_3), .gate(in_2));
  Transistor #(.\type ("n")) transistor_5 (.in(transistor_7_out), .out(out_3), .gate(not_gate_nmos_1_out_2));
  Transistor #(.\type ("n")) transistor_6 (.in(transistor_7_out), .out(out_3), .gate(in_2));
  Transistor #(.\type ("n")) transistor_7 (.in(1'b0), .out(transistor_7_out), .gate(in_1));
  Transistor #(.\type ("n")) transistor_8 (.in(1'b0), .out(transistor_7_out), .gate(not_gate_nmos_2_out_2));

  // Notes on the sheet:
  //   Two input XOR gate
  //   This is the most complex elementary logic gate
endmodule
