// Logisim project basics_memory_units.circ as structural Verilog
module sr_latch (
  input  R,
  input  S,
  output Q,
  output Q_bar
);

  nor nor_1 (Q, R, Q_bar);
  nor nor_2 (Q_bar, Q, S);

  // Notes on the sheet:
  //   An SR latch will initialize to a random value when the circuit is first powered on
  //   The inputs are Set and Reset. Set causes the circuit to latch to an output of 1, Reset causes the output to latch to 0
  //   Only one input is meant to be active at any given time. Behavior for two active inputs is generally treated as undefined
  //   An SR latch is a simple circuit that is designed to be "latched" to a certain output, which will continue after the input is removed
endmodule

module d_flip_flop (
  input  Data_In,
  input  Write,
  output Q,
  output Q_bar
);

  wire nand_1_out, nand_2_out, not_1_out;

  not not_1 (not_1_out, Data_In);
  nand nand_1 (nand_1_out, Data_In, Write);
  nand nand_2 (nand_2_out, Write, not_1_out);
  nand nand_3 (Q, nand_1_out, Q_bar);
  nand nand_4 (Q_bar, Q, nand_2_out);

  // Notes on the sheet:
  //   A D Flip-Flop is similar to a latch, but the value can only be set when the 'write' input is active
endmodule

module rising_edge_d_flip_flop (
  input  Data_In,
  input  Write,
  output Q,
  output Q_bar
);

  wire nand_1_out, nand_2_out, nand_3_out, nand_4_out, nand_5_out, nand_6_out, not_1_out, not_2_out,
       not_3_out, not_4_out;

  not not_1 (not_1_out, Write);
  not not_2 (not_2_out, Data_In);
  nand nand_1 (nand_1_out, Data_In, not_1_out);
  nand nand_2 (nand_2_out, not_1_out, not_2_out);
  nand nand_3 (nand_3_out, nand_1_out, nand_4_out);
  nand nand_4 (nand_4_out, nand_3_out, nand_2_out);
  not not_3 (not_3_out, not_1_out);
  nand nand_5 (nand_5_out, nand_3_out, not_3_out);
  nand nand_6 (nand_6_out, not_3_out, not_4_out);
  not not_4 (not_4_out, nand_3_out);
  nand nand_7 (Q, nand_5_out, Q_bar);
  nand nand_8 (Q_bar, Q, nand_6_out);

  // Notes on the sheet:
  //   Two D flip-flops can be combined to create a flip-flop that only changes its value on a rising-edge when the write input is connected to clock
  //   Series NOT gates from the clock is an intentional choice, to ensure the clock input to the right side of the circuit is active after the left side
endmodule

module four_byte_register (
  input  [7:0] Data_In,
  input  [1:0] Address,
  input  Clock,
  input  Write,
  output [7:0] Data_Out
);

  wire and_1_out, and_2_out, and_3_out, and_4_out, and_5_out, and_6_out, and_7_out, and_8_out, and_9_out,
       and_10_out, and_11_out, and_12_out, and_13_out, and_14_out, and_15_out, and_16_out, and_17_out,
       and_18_out, and_19_out, and_20_out, and_21_out, and_22_out, and_23_out, and_24_out, and_25_out,
       and_26_out, and_27_out, and_28_out, and_29_out, and_30_out, and_31_out, and_32_out, and_33_out,
       and_34_out, and_35_out, and_36_out, d_ff_1_q, d_ff_2_q, d_ff_3_q, d_ff_4_q, d_ff_5_q, d_ff_6_q,
       d_ff_7_q, d_ff_8_q, d_ff_9_q, d_ff_10_q, d_ff_11_q, d_ff_12_q, d_ff_13_q, d_ff_14_q, d_ff_15_q,
       d_ff_16_q, d_ff_17_q, d_ff_18_q, d_ff_19_q, d_ff_20_q, d_ff_21_q, d_ff_22_q, d_ff_23_q, d_ff_24_q,
       d_ff_25_q, d_ff_26_q, d_ff_27_q, d_ff_28_q, d_ff_29_q, d_ff_30_q, d_ff_31_q, d_ff_32_q,
       demultiplexer_1_out0, demultiplexer_1_out1, demultiplexer_1_out2, demultiplexer_1_out3;
  wire [7:0] or_8_out;

  Demultiplexer #(.select(2)) demultiplexer_1 (
    .out0(demultiplexer_1_out0), .out1(demultiplexer_1_out1), .out2(demultiplexer_1_out2),
    .out3(demultiplexer_1_out3), .in(Clock), .sel(Address));
  D_Flip_Flop d_ff_1 (.D(Data_In[7]), .clk(and_1_out), .Q(d_ff_1_q));  // open: Qn, preset, reset
  and and_1 (and_1_out, Write, demultiplexer_1_out0);
  D_Flip_Flop d_ff_2 (.D(Data_In[7]), .clk(and_2_out), .Q(d_ff_2_q));  // open: Qn, preset, reset
  and and_2 (and_2_out, Write, demultiplexer_1_out1);
  D_Flip_Flop d_ff_3 (.D(Data_In[7]), .clk(and_3_out), .Q(d_ff_3_q));  // open: Qn, preset, reset
  and and_3 (and_3_out, Write, demultiplexer_1_out2);
  D_Flip_Flop d_ff_4 (.D(Data_In[7]), .clk(and_4_out), .Q(d_ff_4_q));  // open: Qn, preset, reset
  and and_4 (and_4_out, Write, demultiplexer_1_out3);
  and and_5 (and_5_out, d_ff_4_q, demultiplexer_1_out3);
  and and_6 (and_6_out, demultiplexer_1_out0, d_ff_1_q);
  and and_7 (and_7_out, d_ff_2_q, demultiplexer_1_out1);
  and and_8 (and_8_out, d_ff_3_q, demultiplexer_1_out2);
  or or_1 (or_8_out[7], and_5_out, and_8_out, and_7_out, and_6_out);
  D_Flip_Flop d_ff_5 (.D(Data_In[6]), .clk(and_1_out), .Q(d_ff_5_q));  // open: Qn, preset, reset
  D_Flip_Flop d_ff_6 (.D(Data_In[6]), .clk(and_2_out), .Q(d_ff_6_q));  // open: Qn, preset, reset
  D_Flip_Flop d_ff_7 (.D(Data_In[6]), .clk(and_3_out), .Q(d_ff_7_q));  // open: Qn, preset, reset
  D_Flip_Flop d_ff_8 (.D(Data_In[6]), .clk(and_4_out), .Q(d_ff_8_q));  // open: Qn, preset, reset
  and and_9 (and_9_out, d_ff_6_q, demultiplexer_1_out1);
  and and_10 (and_10_out, d_ff_7_q, demultiplexer_1_out2);
  and and_11 (and_11_out, d_ff_8_q, demultiplexer_1_out3);
  or or_2 (or_8_out[6], and_11_out, and_10_out, and_9_out, and_12_out);
  D_Flip_Flop d_ff_9 (.D(Data_In[5]), .clk(and_1_out), .Q(d_ff_9_q));  // open: Qn, preset, reset
  and and_12 (and_12_out, demultiplexer_1_out0, d_ff_5_q);
  D_Flip_Flop d_ff_10 (.D(Data_In[5]), .clk(and_2_out), .Q(d_ff_10_q));  // open: Qn, preset, reset
  D_Flip_Flop d_ff_11 (.D(Data_In[5]), .clk(and_3_out), .Q(d_ff_11_q));  // open: Qn, preset, reset
  D_Flip_Flop d_ff_12 (.D(Data_In[5]), .clk(and_4_out), .Q(d_ff_12_q));  // open: Qn, preset, reset
  and and_13 (and_13_out, d_ff_12_q, demultiplexer_1_out3);
  and and_14 (and_14_out, demultiplexer_1_out0, d_ff_9_q);
  and and_15 (and_15_out, d_ff_10_q, demultiplexer_1_out1);
  and and_16 (and_16_out, d_ff_11_q, demultiplexer_1_out2);
  or or_3 (or_8_out[5], and_13_out, and_16_out, and_15_out, and_14_out);
  D_Flip_Flop d_ff_13 (.D(Data_In[4]), .clk(and_1_out), .Q(d_ff_13_q));  // open: Qn, preset, reset
  D_Flip_Flop d_ff_14 (.D(Data_In[4]), .clk(and_2_out), .Q(d_ff_14_q));  // open: Qn, preset, reset
  D_Flip_Flop d_ff_15 (.D(Data_In[4]), .clk(and_3_out), .Q(d_ff_15_q));  // open: Qn, preset, reset
  D_Flip_Flop d_ff_16 (.D(Data_In[4]), .clk(and_4_out), .Q(d_ff_16_q));  // open: Qn, preset, reset
  and and_17 (and_17_out, d_ff_14_q, demultiplexer_1_out1);
  and and_18 (and_18_out, d_ff_15_q, demultiplexer_1_out2);
  and and_19 (and_19_out, d_ff_16_q, demultiplexer_1_out3);
  or or_4 (or_8_out[4], and_19_out, and_18_out, and_17_out, and_20_out);
  D_Flip_Flop d_ff_17 (.D(Data_In[3]), .clk(and_1_out), .Q(d_ff_17_q));  // open: Qn, preset, reset
  and and_20 (and_20_out, demultiplexer_1_out0, d_ff_13_q);
  D_Flip_Flop d_ff_18 (.D(Data_In[3]), .clk(and_2_out), .Q(d_ff_18_q));  // open: Qn, preset, reset
  D_Flip_Flop d_ff_19 (.D(Data_In[3]), .clk(and_3_out), .Q(d_ff_19_q));  // open: Qn, preset, reset
  D_Flip_Flop d_ff_20 (.D(Data_In[3]), .clk(and_4_out), .Q(d_ff_20_q));  // open: Qn, preset, reset
  and and_21 (and_21_out, d_ff_20_q, demultiplexer_1_out3);
  and and_22 (and_22_out, demultiplexer_1_out0, d_ff_17_q);
  and and_23 (and_23_out, d_ff_18_q, demultiplexer_1_out1);
  and and_24 (and_24_out, d_ff_19_q, demultiplexer_1_out2);
  or or_5 (or_8_out[3], and_21_out, and_24_out, and_23_out, and_22_out);
  D_Flip_Flop d_ff_21 (.D(Data_In[2]), .clk(and_1_out), .Q(d_ff_21_q));  // open: Qn, preset, reset
  D_Flip_Flop d_ff_22 (.D(Data_In[2]), .clk(and_2_out), .Q(d_ff_22_q));  // open: Qn, preset, reset
  D_Flip_Flop d_ff_23 (.D(Data_In[2]), .clk(and_3_out), .Q(d_ff_23_q));  // open: Qn, preset, reset
  D_Flip_Flop d_ff_24 (.D(Data_In[2]), .clk(and_4_out), .Q(d_ff_24_q));  // open: Qn, preset, reset
  and and_25 (and_25_out, d_ff_22_q, demultiplexer_1_out1);
  and and_26 (and_26_out, d_ff_23_q, demultiplexer_1_out2);
  and and_27 (and_27_out, d_ff_24_q, demultiplexer_1_out3);
  or or_6 (or_8_out[2], and_27_out, and_26_out, and_25_out, and_28_out);
  D_Flip_Flop d_ff_25 (.D(Data_In[1]), .clk(and_1_out), .Q(d_ff_25_q));  // open: Qn, preset, reset
  and and_28 (and_28_out, demultiplexer_1_out0, d_ff_21_q);
  D_Flip_Flop d_ff_26 (.D(Data_In[1]), .clk(and_2_out), .Q(d_ff_26_q));  // open: Qn, preset, reset
  D_Flip_Flop d_ff_27 (.D(Data_In[1]), .clk(and_3_out), .Q(d_ff_27_q));  // open: Qn, preset, reset
  D_Flip_Flop d_ff_28 (.D(Data_In[1]), .clk(and_4_out), .Q(d_ff_28_q));  // open: Qn, preset, reset
  and and_29 (and_29_out, d_ff_28_q, demultiplexer_1_out3);
  and and_30 (and_30_out, demultiplexer_1_out0, d_ff_25_q);
  and and_31 (and_31_out, d_ff_26_q, demultiplexer_1_out1);
  and and_32 (and_32_out, d_ff_27_q, demultiplexer_1_out2);
  or or_7 (or_8_out[1], and_29_out, and_32_out, and_31_out, and_30_out);
  D_Flip_Flop d_ff_29 (.D(Data_In[0]), .clk(and_1_out), .Q(d_ff_29_q));  // open: Qn, preset, reset
  D_Flip_Flop d_ff_30 (.D(Data_In[0]), .clk(and_2_out), .Q(d_ff_30_q));  // open: Qn, preset, reset
  D_Flip_Flop d_ff_31 (.D(Data_In[0]), .clk(and_3_out), .Q(d_ff_31_q));  // open: Qn, preset, reset
  D_Flip_Flop d_ff_32 (.D(Data_In[0]), .clk(and_4_out), .Q(d_ff_32_q));  // open: Qn, preset, reset
  and and_33 (and_33_out, d_ff_30_q, demultiplexer_1_out1);
  and and_34 (and_34_out, d_ff_31_q, demultiplexer_1_out2);
  and and_35 (and_35_out, d_ff_32_q, demultiplexer_1_out3);
  or or_8 (or_8_out[0], and_35_out, and_34_out, and_33_out, and_36_out);
  and and_36 (and_36_out, demultiplexer_1_out0, d_ff_29_q);
  Multiplexer #(.width(8)) multiplexer_1 (.in0(or_8_out), .in1({8{1'b0}}), .out(Data_Out), .sel(Write));

  // Notes on the sheet:
  //   Write if 1, read if 0
endmodule

module sixteen_byte_register (
  input  [7:0] Data_In,
  input  [3:0] Address,
  input  Clock,
  input  Write,
  output [7:0] Data_Out
);

  wire demultiplexer_1_out0, demultiplexer_1_out1, demultiplexer_1_out2, demultiplexer_1_out3;
  wire [7:0] four_byte_register_1_data_out, four_byte_register_2_data_out, four_byte_register_3_data_out,
       four_byte_register_4_data_out;

  Demultiplexer #(.select(2)) demultiplexer_1 (
    .out0(demultiplexer_1_out0), .out1(demultiplexer_1_out1), .out2(demultiplexer_1_out2),
    .out3(demultiplexer_1_out3), .in(Clock), .sel(Address[3:2]));
  four_byte_register four_byte_register_1 (
    .Data_In(Data_In), .Address(Address[1:0]), .Clock(demultiplexer_1_out0), .Write(Write),
    .Data_Out(four_byte_register_1_data_out));
  four_byte_register four_byte_register_2 (
    .Data_In(Data_In), .Address(Address[1:0]), .Clock(demultiplexer_1_out1), .Write(Write),
    .Data_Out(four_byte_register_2_data_out));
  four_byte_register four_byte_register_3 (
    .Data_In(Data_In), .Address(Address[1:0]), .Clock(demultiplexer_1_out2), .Write(Write),
    .Data_Out(four_byte_register_3_data_out));
  four_byte_register four_byte_register_4 (
    .Data_In(Data_In), .Address(Address[1:0]), .Clock(demultiplexer_1_out3), .Write(Write),
    .Data_Out(four_byte_register_4_data_out));
  assign Data_Out = four_byte_register_1_data_out | four_byte_register_2_data_out | four_byte_register_3_data_out | four_byte_register_4_data_out;  // OR_Gate or_1, 8 bits wide
endmodule

module sixty_four_byte_register (
  input  [7:0] Data_In,
  input  [5:0] Address,
  input  Clock,
  input  Write,
  output [7:0] Data_Out
);

  wire demultiplexer_1_out0, demultiplexer_1_out1, demultiplexer_1_out2, demultiplexer_1_out3;
  wire [7:0] sixteen_byte_register_1_data_out, sixteen_byte_register_2_data_out,
       sixteen_byte_register_3_data_out, sixteen_byte_register_4_data_out;

  Demultiplexer #(.select(2)) demultiplexer_1 (
    .out0(demultiplexer_1_out0), .out1(demultiplexer_1_out1), .out2(demultiplexer_1_out2),
    .out3(demultiplexer_1_out3), .in(Clock), .sel(Address[5:4]));
  sixteen_byte_register sixteen_byte_register_1 (
    .Data_In(Data_In), .Address(Address[3:0]), .Clock(demultiplexer_1_out0), .Write(Write),
    .Data_Out(sixteen_byte_register_1_data_out));
  sixteen_byte_register sixteen_byte_register_2 (
    .Data_In(Data_In), .Address(Address[3:0]), .Clock(demultiplexer_1_out1), .Write(Write),
    .Data_Out(sixteen_byte_register_2_data_out));
  sixteen_byte_register sixteen_byte_register_3 (
    .Data_In(Data_In), .Address(Address[3:0]), .Clock(demultiplexer_1_out2), .Write(Write),
    .Data_Out(sixteen_byte_register_3_data_out));
  sixteen_byte_register sixteen_byte_register_4 (
    .Data_In(Data_In), .Address(Address[3:0]), .Clock(demultiplexer_1_out3), .Write(Write),
    .Data_Out(sixteen_byte_register_4_data_out));
  assign Data_Out = sixteen_byte_register_1_data_out | sixteen_byte_register_2_data_out | sixteen_byte_register_3_data_out | sixteen_byte_register_4_data_out;  // OR_Gate or_1, 8 bits wide
endmodule

module two_fixty_six_byte_register (
  input  [7:0] Data_In,
  input  [7:0] Address,
  input  Clock,
  input  Write,
  output [7:0] Data_Out
);

  wire demultiplexer_1_out0, demultiplexer_1_out1, demultiplexer_1_out2, demultiplexer_1_out3;
  wire [7:0] sixty_four_byte_register_1_data_out, sixty_four_byte_register_2_data_out,
       sixty_four_byte_register_3_data_out, sixty_four_byte_register_4_data_out;

  Demultiplexer #(.select(2)) demultiplexer_1 (
    .out0(demultiplexer_1_out0), .out1(demultiplexer_1_out1), .out2(demultiplexer_1_out2),
    .out3(demultiplexer_1_out3), .in(Clock), .sel(Address[7:6]));
  sixty_four_byte_register sixty_four_byte_register_1 (
    .Data_In(Data_In), .Address(Address[5:0]), .Clock(demultiplexer_1_out0), .Write(Write),
    .Data_Out(sixty_four_byte_register_1_data_out));
  sixty_four_byte_register sixty_four_byte_register_2 (
    .Data_In(Data_In), .Address(Address[5:0]), .Clock(demultiplexer_1_out1), .Write(Write),
    .Data_Out(sixty_four_byte_register_2_data_out));
  sixty_four_byte_register sixty_four_byte_register_3 (
    .Data_In(Data_In), .Address(Address[5:0]), .Clock(demultiplexer_1_out2), .Write(Write),
    .Data_Out(sixty_four_byte_register_3_data_out));
  sixty_four_byte_register sixty_four_byte_register_4 (
    .Data_In(Data_In), .Address(Address[5:0]), .Clock(demultiplexer_1_out3), .Write(Write),
    .Data_Out(sixty_four_byte_register_4_data_out));
  assign Data_Out = sixty_four_byte_register_1_data_out | sixty_four_byte_register_2_data_out | sixty_four_byte_register_3_data_out | sixty_four_byte_register_4_data_out;  // OR_Gate or_1, 8 bits wide
endmodule
